// Logisim project 1.3.3.2.circ as structural Verilog: 2 circuits, main circuit main
module main (
  input  in_1,
  input  in_2,
  input  in_3,
  input  in_4,
  input  in_5,
  input  in_6,
  input  in_7,
  input  in_8,
  output out_9,
  output out_10,
  output out_11,
  output out_12,
  output out_13
);

  _4_bit_adder u_4_bit_adder_1 (
    .in_2(in_1), .in_3(in_2), .in_4(in_3), .in_5(in_4), .in_6(in_5), .in_7(in_6), .in_8(in_7), .in_9(in_8),
    .in_1(1'b0), .out_14(out_13), .out_10(out_9), .out_11(out_10), .out_12(out_11), .out_13(out_12));
endmodule

module _4_bit_adder (
  input  in_1,
  input  in_2,
  input  in_3,
  input  in_4,
  input  in_5,
  input  in_6,
  input  in_7,
  input  in_8,
  input  in_9,
  output out_10,
  output out_11,
  output out_12,
  output out_13,
  output out_14
);

  wire full_adder_1_out_5, full_adder_2_out_5, full_adder_3_out_5;

  full_adder full_adder_1 (.in_2(in_6), .in_3(in_2), .in_1(in_1), .out_5(full_adder_1_out_5), .out_4(out_10));
  full_adder full_adder_2 (
    .in_2(in_7), .in_3(in_3), .in_1(full_adder_1_out_5), .out_5(full_adder_2_out_5), .out_4(out_11));
  full_adder full_adder_3 (
    .in_2(in_8), .in_3(in_4), .in_1(full_adder_2_out_5), .out_5(full_adder_3_out_5), .out_4(out_12));
  full_adder full_adder_4 (.in_2(in_9), .in_3(in_5), .in_1(full_adder_3_out_5), .out_5(out_14), .out_4(out_13));
endmodule
