// Logisim project 1.4.2+3 bis.circ as structural Verilog: 1 circuit, main circuit main
module main (
  output out_1,
  output out_2,
  output out_3,
  output out_4
);

  wire clock_1_out, d_ff_1_q, d_ff_2_q, d_ff_3_q, d_ff_4_q;

  Clock clock_1 (.out(clock_1_out));
  D_Flip_Flop d_ff_1 (.clk(clock_1_out), .D(out_1), .Q(d_ff_1_q));  // open: Qn, preset, en, reset
  D_Flip_Flop d_ff_2 (.clk(clock_1_out), .D(out_2), .Q(d_ff_2_q));  // open: Qn, preset, en, reset
  increment increment_1 (
    .in_1(d_ff_1_q), .in_2(d_ff_2_q), .in_3(d_ff_3_q), .in_4(d_ff_4_q), .out_5(out_1), .out_6(out_2),
    .out_7(out_3), .out_8(out_4));
  D_Flip_Flop d_ff_3 (.clk(clock_1_out), .D(out_3), .Q(d_ff_3_q));  // open: Qn, preset, en, reset
  D_Flip_Flop d_ff_4 (.clk(clock_1_out), .D(out_4), .Q(d_ff_4_q));  // open: Qn, preset, en, reset
endmodule
