// Logisim project 1.5.3.circ as structural Verilog: 1 circuit, main circuit main
module main (
  input  in_1,
  input  in_2,
  output out_3,
  output out_4,
  output out_5,
  output out_6,
  output out_7
);

  wire and_1_out, clock_1_out;
  wire [4:0] register_1_q;

  Clock clock_1 (.out(clock_1_out));
  and and_1 (and_1_out, clock_1_out, in_1);
  Register #(.width(5)) register_1 (
    .D({in_2, out_6, out_5, out_4, out_3}), .Q(register_1_q), .clk(and_1_out));  // open: en, clr
  _4_bit_adder u_4_bit_adder_1 (
    .in_2(register_1_q[0]), .in_3(register_1_q[1]), .in_4(register_1_q[2]), .in_5(register_1_q[3]),
    .in_6(1'b1), .in_7(register_1_q[4]), .in_8(register_1_q[4]), .in_9(register_1_q[4]), .in_1(1'b0),
    .out_14(out_7), .out_10(out_3), .out_11(out_4), .out_12(out_5), .out_13(out_6));
endmodule
